# Fritzing sketch lilypad (saved by Fritzing 0.9.2b)

parts:
  Part2 = LilyPad Arduino Simple Board
  Part3 = LilyPad LED
  Part4 = LilyPad LED
  Part5 = LilyPad LED
  Part6 = LilyPad LED
  Part8 = LilyPad LED
  Part9 = LilyPad LED
  Part10 = LilyPad LED
  Part11 = LilyPad LED
  Part12 = LilyPad LED
  Part13 = LilyPad LED
  Part14 = LilyPad Accelerometer ADXL335

nets:
  N1: Part2.A2, Part6.+, Part10.+
  N2: Part2.A3, Part14.XOUT
  N3: Part2.A4, Part14.YOUT
  N4: Part2.A5, Part14.ZOUT
  N5: Part2.D11, Part4.+, Part11.+
  N6: Part2.D6, Part8.+
  N7: Part2.D9, Part5.+
  N8: Part2.D10, Part3.+, Part12.+
  N9: Part2.D5, Part13.+
  N10: Part2.GND, Part3.-, Part4.-, Part5.-, Part6.-, Part8.-, Part9.-, Part10.-, Part11.-, Part12.-, Part13.-, Part14.COM
  VCC: Part2.VCC, Part14.5V
